# Fritzing sketch KARR (saved by Fritzing 0.4.3b)
breadboards: 1

parts:
  Arduino1 = Arduino Mega
  R0 = Resistor [resistance=220 package=THT]
  R1 = Resistor [resistance=220 package=THT]
  R2 = Resistor [resistance=220 package=THT]
  R3 = Resistor [resistance=220 package=THT]
  R4 = Resistor [resistance=220 package=THT]
  R5 = Resistor [resistance=220 package=THT]
  R6 = Resistor [resistance=220 package=THT]
  R7 = Resistor [resistance=220 package=THT]
  R8 = Resistor [resistance=220 package=THT]
  R9 = Resistor [resistance=220 package=THT]
  LED0 = yellow LED - 5mm
  LED1 = yellow LED - 5mm
  LED2 = yellow LED - 5mm
  LED3 = yellow LED - 5mm
  LED4 = yellow LED - 5mm
  LED5 = yellow LED - 5mm
  LED6 = yellow LED - 5mm
  LED7 = yellow LED - 5mm
  LED8 = yellow LED - 5mm
  LED9 = yellow LED - 5mm

nets:
  N1: Arduino1.GND, LED0.cathode, LED1.cathode, LED2.cathode, LED3.cathode, LED4.cathode, LED5.cathode, LED6.cathode, LED7.cathode, LED8.cathode, LED9.cathode
  N2: Arduino1.D13, R0.Pin_1
  N3: Arduino1.D12, R1.Pin_1
  N4: Arduino1.D11, R2.Pin_1
  N5: Arduino1.D10, R3.Pin_1
  N6: Arduino1.D9, R4.Pin_1
  N7: Arduino1.D8, R5.Pin_1
  N8: Arduino1.D7, R6.Pin_1
  N9: Arduino1.D6, R7.Pin_1
  N10: Arduino1.D5, R8.Pin_1
  N11: Arduino1.D4, R9.Pin_1
  N12: R0.Pin_0, LED0.anode
  N13: R1.Pin_0, LED1.anode
  N14: R2.Pin_0, LED2.anode
  N15: R3.Pin_0, LED3.anode
  N16: R4.Pin_0, LED4.anode
  N17: R5.Pin_0, LED5.anode
  N18: R6.Pin_0, LED6.anode
  N19: R7.Pin_0, LED7.anode
  N20: R8.Pin_0, LED8.anode
  N21: R9.Pin_0, LED9.anode
